# Fritzing sketch Tåg (saved by Fritzing 0.9.1b)
breadboards: 1

parts:
  Arduino = Arduino Uno (Rev3)
  R1 = Resistor [tolerance=±5% resistance=470 package=THT]
  1_1 = Pushbutton [package=THT]
  1_2 = Pushbutton [package=THT]
  1_3 = Pushbutton [package=THT]
  2_1 = Pushbutton [package=THT]
  2_2 = Pushbutton [package=THT]
  2_3 = Pushbutton [package=THT]
  3_1 = Pushbutton [package=THT]
  S8 = Pushbutton [package=THT]
  S9 = Pushbutton [package=THT]
  D1 = Rectifier Diode [part_number=1N4001 package="300 mil [THT]"]
  Q1 = NPN-Transistor [package="TO92 [THT]"]
  M1 = DC Motor
  D2 = Rectifier Diode [part_number=1N4001 package="300 mil [THT]"]
  Q2 = NPN-Transistor [package="TO92 [THT]"]
  M2 = DC Motor
  D3 = Rectifier Diode [part_number=1N4001 package="300 mil [THT]"]
  Q3 = NPN-Transistor [package="TO92 [THT]"]
  M3 = DC Motor
  S10 = Pushbutton [package=THT]

nets:
  N1: Arduino.D8, 1_1.leg0, 1_2.leg0, 1_3.leg0
  N2: Arduino.D9_PWM, 2_1.leg0, 2_2.leg0, 2_3.leg0
  N3: Arduino.D10_PWM/SS, 3_1.leg0, S8.leg0, S9.leg0
  N4: Arduino.GND, M1.pin_2, M2.pin_2, M3.pin_2
  N5: Arduino.D0/RX, S10.leg0
  N6: Arduino.D3_PWM, D3.anode
  N7: Arduino.D5_PWM, D2.anode
  N8: Arduino.D6_PWM, D1.anode
  N9: Arduino.5V, R1.Pin_0
  N10: R1.Pin_1, 1_1.leg1, 1_2.leg1, 1_3.leg1, 2_1.leg1, 2_2.leg1, 2_3.leg1, 3_1.leg1, S8.leg1, S9.leg1, S10.leg1
  N11: D1.cathode, Q1.B
  N12: Q1.E, M1.pin_1
  5V: Q1.C, Q2.C, Q3.C
  N13: D2.cathode, Q2.B
  N14: Q2.E, M2.pin_1
  N15: D3.cathode, Q3.B
  N16: Q3.E, M3.pin_1
